# Fritzing sketch amp_player (saved by Fritzing 1.0.0rc)
breadboards: 2

parts:
  Part10 = Adafruit MAX98306 Stereo 3.7W Class D Audio Amplifier [part_number="Adafruit #987"]
  R9 = Rotary Potentiometer (Small) [maximum_resistance=10kΩ knob_status=50% power=0.5W package=THT]
  SP1 = SPEAKER [package=pcb_mount_speaker]
  A2 = DFPlayer Pro-a mini

nets:
  N1: Part10.LOUT-, SP1.+
  N2: Part10.LOUT+, SP1.-
  N3: Part10.IN_LEFT-, R9.leg1, A2.Pin_8
  N4: Part10.IN_LEFT+, R9.wiper
  N5: Part10.GND, A2.Pin_2
  N6: Part10.VDD, A2.Pin_1
  N7: R9.leg2, A2.Pin_7

custom parts:
  Adafruit MAX98306 Stereo 3.7W Class D Audio Amplifier: This incredibly small stereo amplifier is surprisingly powerful - able to deliver 2 x 3.7W channels into 3 ohm impedance speakers. Inside the miniature chip is a class D controller, able to run from 2.7V-5.5VDC. Since the amp is a class D, its incredibly efficient (over 90% efficient when driving an 8Ω speaker at over a Watt) - making it perfect for portable and battery-powered projects. It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
  DFPlayer Pro-a mini: DFPlayer Pro-a mini simple but powerful MP3 Player.
