# Fritzing sketch osc_seq_mix_tones (saved by Fritzing 1.0.4)
breadboards: 6

parts:
  U3 = 4046 [chip_label=4046 package="DIP (Dual Inline) [THT]"]
  R11 = Resistor [tolerance=±5% resistance=10k package="1206 [SMD]"]
  C3 = Capacitor [package=cap-pth-large]
  POT4 = Breadboard Trimpot
  SP3 = SPEAKER [package=pcb_mount_speaker]
  Part13 = Adafruit MAX98306 Stereo 3.7W Class D Audio Amplifier [part_number="Adafruit #987"]
  Part14 = BH Adafruit JST-PH Breakout
  POT5 = Breadboard Trimpot
  U4 = 4046 [chip_label=4046 package="DIP (Dual Inline) [THT]"]
  R12 = Resistor [tolerance=±5% resistance=10k package="1206 [SMD]"]
  C4 = Capacitor [package=cap-pth-large]
  U5 = 4017 [chip_label=4017 package="DIP (Dual Inline) [THT]"]
  R13 = Resistor [tolerance=±5% resistance=2.2k package="0603 [SMD]"]
  LED2 = LED - 3mm [color="Red (633nm)" current=0.030A package="3 mm [THT]"]
  D6 = Rectifier Diode [part_number=1N4001 package="300 mil [THT]"]
  D7 = Rectifier Diode [part_number=1N4001 package="300 mil [THT]"]
  D8 = Rectifier Diode [part_number=1N4001 package="300 mil [THT]"]
  POT10 = Breadboard Trimpot
  POT11 = Breadboard Trimpot
  POT12 = Breadboard Trimpot

nets:
  N1: U3.pin4, U5.pin14
  N2: U3.pin5, U3.pin8, R11.Pin_0, POT4.PIN3, Part13.IN_LEFT-, Part13.GND, Part14.V+, POT5.PIN3, U4.pin5, U4.pin8, R12.Pin_0, U5.pin8, U5.pin13, LED2.cathode, POT10.PIN3, POT11.PIN3, POT12.PIN3
  N3: U3.pin6, C3.1
  N4: U3.pin7, C3.2
  N5: U3.pin9, POT4.PIN2
  N6: U3.pin11, R11.Pin_1
  N7: U3.pin16, POT4.PIN1, Part13.VDD, Part14.SW, U4.pin16, U5.pin16
  N8: SP3.+, Part13.LOUT-
  N9: SP3.-, Part13.LOUT+
  N10: Part13.IN_LEFT+, POT5.PIN2
  N11: POT5.PIN1, U4.pin4
  N12: U4.pin6, C4.1
  N13: U4.pin7, C4.2
  N14: U4.pin9, D6.cathode, D7.cathode, D8.cathode
  N15: U4.pin11, R12.Pin_1
  N16: U5.pin3, R13.Pin_1, POT10.PIN1
  N17: U5.pin5, POT11.PIN1
  N18: U5.pin9, U5.pin15
  N19: U5.pin10, POT12.PIN1
  N20: R13.Pin_0, LED2.anode
  N21: D6.anode, POT11.PIN2
  N22: D7.anode, POT10.PIN2
  N23: D8.anode, POT12.PIN2

custom parts:
  4046: 4017 CMOS decade counter with 10 decoded outputs
  Adafruit MAX98306 Stereo 3.7W Class D Audio Amplifier: This incredibly small stereo amplifier is surprisingly powerful - able to deliver 2 x 3.7W channels into 3 ohm impedance speakers. Inside the miniature chip is a class D controller, able to run from 2.7V-5.5VDC. Since the amp is a class D, its incredibly efficient (over 90% efficient when driving an 8Ω speaker at over a Watt) - making it perfect for portable and battery-powered projects. It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
  BH Adafruit JST-PH Breakout: This switched JST connector is the best way to quickly prototype with our LiPoly batteries. We paired a genuine JST connector with a slide switch that can do up to 600mA. Both are soldered onto a breadboard-friendly breakout. There's two ground pins, one 'switched' power pin, and one pin that is always on. This is compatible with the "JST PH 2-pin" connectors we use in our battery packs..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
  4017: 4017 CMOS decade counter with 10 decoded outputs
