# Fritzing sketch player_button (saved by Fritzing 1.0.0rc)
breadboards: 1

parts:
  A1 = DFPlayer Pro-a mini
  S1 = Momentary Switch [package=ksa_sealed_tac_switch]

nets:
  N1: A1.Pin_2, S1.1
  N2: A1.Pin_12, S1.3

custom parts:
  DFPlayer Pro-a mini: DFPlayer Pro-a mini simple but powerful MP3 Player.
