# Fritzing sketch synth_base (saved by Fritzing 1.0.4)
breadboards: 2

parts:
  SP2 = SPEAKER [package=pcb_mount_speaker]
  Part11 = Adafruit MAX98306 Stereo 3.7W Class D Audio Amplifier [part_number="Adafruit #987"]
  Part12 = BH Adafruit JST-PH Breakout
  POT3 = Breadboard Trimpot

nets:
  N1: SP2.+, Part11.LOUT-
  N2: SP2.-, Part11.LOUT+
  N3: Part11.IN_LEFT-, Part11.GND, Part12.V+, POT3.PIN3
  N4: Part11.IN_LEFT+, POT3.PIN2
  N5: Part11.VDD, Part12.SW

custom parts:
  Adafruit MAX98306 Stereo 3.7W Class D Audio Amplifier: This incredibly small stereo amplifier is surprisingly powerful - able to deliver 2 x 3.7W channels into 3 ohm impedance speakers. Inside the miniature chip is a class D controller, able to run from 2.7V-5.5VDC. Since the amp is a class D, its incredibly efficient (over 90% efficient when driving an 8Ω speaker at over a Watt) - making it perfect for portable and battery-powered projects. It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
  BH Adafruit JST-PH Breakout: This switched JST connector is the best way to quickly prototype with our LiPoly batteries. We paired a genuine JST connector with a slide switch that can do up to 600mA. Both are soldered onto a breadboard-friendly breakout. There's two ground pins, one 'switched' power pin, and one pin that is always on. This is compatible with the "JST PH 2-pin" connectors we use in our battery packs..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
