# Fritzing sketch tone_control (saved by Fritzing 1.0.4)
breadboards: 1

parts:
  POT7 = Breadboard Trimpot
  POT8 = Breadboard Trimpot
  POT9 = Breadboard Trimpot
  D3 = Rectifier Diode [part_number=1N4001 package="300 mil [THT]"]
  D4 = Rectifier Diode [part_number=1N4001 package="300 mil [THT]"]
  D5 = Rectifier Diode [part_number=1N4001 package="300 mil [THT]"]

nets:
  N1: POT7.PIN2, D4.anode
  N2: POT7.PIN3, POT8.PIN3, POT9.PIN3
  N3: POT8.PIN2, D3.anode
  N4: POT9.PIN2, D5.anode
  N5: D3.cathode, D4.cathode, D5.cathode
