# Fritzing sketch vco (saved by Fritzing 1.0.4)
breadboards: 1

parts:
  U2 = 4046 [chip_label=4046 package="DIP (Dual Inline) [THT]"]
  R10 = Resistor [tolerance=±5% resistance=10k package="1206 [SMD]"]
  C2 = Capacitor [package=cap-pth-large]
  POT3 = Breadboard Trimpot

nets:
  N1: U2.pin5, U2.pin8, R10.Pin_0, POT3.PIN3
  N2: U2.pin6, C2.1
  N3: U2.pin7, C2.2
  N4: U2.pin9, POT3.PIN2
  N5: U2.pin11, R10.Pin_1
  N6: U2.pin16, POT3.PIN1

custom parts:
  4046: 4017 CMOS decade counter with 10 decoded outputs
