# Fritzing sketch mixer (saved by Fritzing 1.0.0rc)
breadboards: 1

parts:
  D1 = Rectifier Diode [part_number=1N4001 package="300 mil [THT]"]
  D2 = Rectifier Diode [part_number=1N4001 package="300 mil [THT]"]

nets:
  N1: D1.cathode, D2.cathode
