# Fritzing sketch setup (saved by Fritzing 1.0.0rc)
breadboards: 3

parts:
  Part1 = Adafruit MAX98306 Stereo 3.7W Class D Audio Amplifier [part_number="Adafruit #987"]
  U2 = 4046 [chip_label=4046 package="DIP (Dual Inline) [THT]"]
  C1 = Electrolytic Capacitor [capacitance=0.1µF voltage=10V package="0605 [SMD, electrolytic]"]
  R1 = Resistor [tolerance=±5% power=0.25W resistance=10k package=THT]
  Part3 = BH Adafruit JST-PH Breakout
  POT1 = Breadboard Trimpot
  POT2 = Breadboard Trimpot
  U3 = 4046 [chip_label=4046 package="DIP (Dual Inline) [THT]"]
  C2 = Electrolytic Capacitor [capacitance=0.1µF voltage=10V package="0605 [SMD, electrolytic]"]
  R2 = Resistor [tolerance=±5% power=0.25W resistance=10k package=THT]
  Part4 = BH Adafruit JST-PH Breakout
  Part5 = Adafruit MAX98306 Stereo 3.7W Class D Audio Amplifier [part_number="Adafruit #987"]
  POT3 = Breadboard Trimpot
  R3 = PHOTOCELL [package=photocell-kit]
  R4 = Resistor [tolerance=±5% power=0.25W resistance=10k package=THT]
  U4 = 4046 [chip_label=4046 package="DIP (Dual Inline) [THT]"]
  C3 = Electrolytic Capacitor [capacitance=0.1µF voltage=10V package="0605 [SMD, electrolytic]"]
  R5 = Resistor [tolerance=±5% power=0.25W resistance=10k package=THT]
  Part6 = BH Adafruit JST-PH Breakout
  Part7 = Adafruit MAX98306 Stereo 3.7W Class D Audio Amplifier [part_number="Adafruit #987"]
  POT4 = Breadboard Trimpot

nets:
  N1: Part1.IN_LEFT-, Part1.GND, U2.pin5, U2.pin8, R1.Pin_0, Part3.V+, POT1.PIN3, POT2.PIN3
  N2: Part1.IN_LEFT+, POT1.PIN2
  N3: Part1.VDD, U2.pin16, Part3.SW, POT2.PIN1
  N4: U2.pin4, POT1.PIN1
  N5: U2.pin6, C1.+
  N6: U2.pin7, C1.-
  N7: U2.pin9, POT2.PIN2
  N8: U2.pin11, R1.Pin_1
  N9: U3.pin4, POT3.PIN1
  N10: U3.pin5, U3.pin8, R2.Pin_0, Part4.V+, Part5.IN_LEFT-, Part5.GND, POT3.PIN3, R4.Pin_1
  N11: U3.pin6, C2.+
  N12: U3.pin7, C2.-
  N13: U3.pin9, R3.P$2, R4.Pin_0
  N14: U3.pin11, R2.Pin_1
  N15: U3.pin16, Part4.SW, Part5.VDD, R3.P$1
  N16: Part5.IN_LEFT+, POT3.PIN2
  N17: U4.pin4, POT4.PIN1
  N18: U4.pin5, U4.pin8, R5.Pin_0, Part6.V+, Part7.IN_LEFT-, Part7.GND, POT4.PIN3
  N19: U4.pin6, C3.+
  N20: U4.pin7, C3.-
  N21: U4.pin11, R5.Pin_1
  N22: U4.pin16, Part6.SW, Part7.VDD
  N23: Part7.IN_LEFT+, POT4.PIN2

custom parts:
  Adafruit MAX98306 Stereo 3.7W Class D Audio Amplifier: This incredibly small stereo amplifier is surprisingly powerful - able to deliver 2 x 3.7W channels into 3 ohm impedance speakers. Inside the miniature chip is a class D controller, able to run from 2.7V-5.5VDC. Since the amp is a class D, its incredibly efficient (over 90% efficient when driving an 8Ω speaker at over a Watt) - making it perfect for portable and battery-powered projects. It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
  4046: 4017 CMOS decade counter with 10 decoded outputs
  BH Adafruit JST-PH Breakout: This switched JST connector is the best way to quickly prototype with our LiPoly batteries. We paired a genuine JST connector with a slide switch that can do up to 600mA. Both are soldered onto a breadboard-friendly breakout. There's two ground pins, one 'switched' power pin, and one pin that is always on. This is compatible with the "JST PH 2-pin" connectors we use in our battery packs..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
