# Fritzing sketch vco_sensor (saved by Fritzing 1.0.0rc)
breadboards: 1

parts:
  U3 = 4046 [chip_label=4046 package="DIP (Dual Inline) [THT]"]
  R5 = Resistor [tolerance=±5% resistance=10k package="1206 [SMD]"]
  R6 = Resistor [tolerance=±5% resistance=2.2k package="1206 [SMD]"]
  C3 = Capacitor [package=cap-pth-large]
  R7 = PHOTOCELL [package=photocell-kit]

nets:
  N1: U3.pin5, U3.pin8, R5.Pin_0, R6.Pin_1
  N2: U3.pin6, C3.1
  N3: U3.pin7, C3.2
  N4: U3.pin9, R6.Pin_0, R7.P$2
  N5: U3.pin11, R5.Pin_1
  N6: U3.pin16, R7.P$1

custom parts:
  4046: 4017 CMOS decade counter with 10 decoded outputs
