# Fritzing sketch VCO copy (saved by Fritzing 1.0.0rc)
breadboards: 5

parts:
  U1 = 4046 [chip_label=4046 package="DIP (Dual Inline) [THT]"]
  C1 = Capacitor [package=cap-pth-large]
  R1 = Resistor [tolerance=±5% resistance=10k package="1206 [SMD]"]
  U2 = 4046 [chip_label=4046 package="DIP (Dual Inline) [THT]"]
  R2 = Resistor [tolerance=±5% resistance=10k package="1206 [SMD]"]
  C2 = Capacitor [package=cap-pth-large]
  R3 = PHOTOCELL [package=photocell-kit]
  R4 = Resistor [tolerance=±5% resistance=2.2k package="1206 [SMD]"]
  U3 = 4017 [chip_label=4017 package="DIP (Dual Inline) [THT]"]
  LED1 = smd LED [color="Red (633nm)" package="0603 [SMD]"]
  R5 = Resistor [tolerance=±5% resistance=10k package="1206 [SMD]"]
  R6 = Rotary Potentiometer (Large) [maximum_resistance=10kΩ knob_status=50% power=0.5W package=THT]
  Part1 = Adafruit MAX98306 Stereo 3.7W Class D Audio Amplifier [part_number="Adafruit #987"]
  Part8 = BH Adafruit JST-PH Breakout
  C3 = Capacitor [package=cap-pth-large]
  Part9 = Adafruit MAX98306 Stereo 3.7W Class D Audio Amplifier [part_number="Adafruit #987"]
  C4 = Capacitor [package=cap-pth-large]
  R8 = Rotary Potentiometer (Small) [maximum_resistance=10kΩ knob_status=50% power=0.5W package=THT]
  R9 = Rotary Potentiometer (Small) [maximum_resistance=10kΩ knob_status=50% power=0.5W package=THT]

nets:
  N1: U1.pin5, U1.pin8, R1.Pin_0, R9.leg2
  N2: U1.pin6, C1.1
  N3: U1.pin7, C1.2
  N4: U1.pin9, R9.wiper
  N5: U1.pin11, R1.Pin_1
  N6: U1.pin16, R9.leg1
  N7: U2.pin5, U2.pin8, R2.Pin_0, R4.Pin_1
  N8: U2.pin6, C2.1
  N9: U2.pin7, C2.2
  N10: U2.pin9, R3.P$2, R4.Pin_0
  N11: U2.pin11, R2.Pin_1
  N12: U2.pin16, R3.P$1
  N13: U3.pin3, R5.Pin_1
  N14: U3.pin8, U3.pin13, LED1.cathode
  N15: U3.pin9, U3.pin15
  N16: LED1.anode, R5.Pin_0
  N17: R6.leg1, Part1.IN_LEFT-, Part1.GND, Part8.V+, C3.2
  N18: R6.wiper, Part1.IN_LEFT+
  N19: R6.leg2, C3.1
  N20: Part1.VDD, Part8.SW
  N21: Part9.IN_LEFT-, Part9.GND, C4.2, R8.leg1
  N22: Part9.IN_LEFT+, R8.wiper
  N23: C4.1, R8.leg2

custom parts:
  4046: 4017 CMOS decade counter with 10 decoded outputs
  4017: 4017 CMOS decade counter with 10 decoded outputs
  Adafruit MAX98306 Stereo 3.7W Class D Audio Amplifier: This incredibly small stereo amplifier is surprisingly powerful - able to deliver 2 x 3.7W channels into 3 ohm impedance speakers. Inside the miniature chip is a class D controller, able to run from 2.7V-5.5VDC. Since the amp is a class D, its incredibly efficient (over 90% efficient when driving an 8Ω speaker at over a Watt) - making it perfect for portable and battery-powered projects. It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
  BH Adafruit JST-PH Breakout: This switched JST connector is the best way to quickly prototype with our LiPoly batteries. We paired a genuine JST connector with a slide switch that can do up to 600mA. Both are soldered onto a breadboard-friendly breakout. There's two ground pins, one 'switched' power pin, and one pin that is always on. This is compatible with the "JST PH 2-pin" connectors we use in our battery packs..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
