# Fritzing sketch amp (saved by Fritzing 1.0.0rc)
breadboards: 1

parts:
  Part10 = Adafruit MAX98306 Stereo 3.7W Class D Audio Amplifier [part_number="Adafruit #987"]
  C5 = Capacitor [package=cap-pth-large]
  R9 = Rotary Potentiometer (Small) [maximum_resistance=10kΩ knob_status=50% power=0.5W package=THT]

nets:
  N1: Part10.IN_LEFT-, Part10.GND, C5.2, R9.leg1
  N2: Part10.IN_LEFT+, R9.wiper
  N3: C5.1, R9.leg2

custom parts:
  Adafruit MAX98306 Stereo 3.7W Class D Audio Amplifier: This incredibly small stereo amplifier is surprisingly powerful - able to deliver 2 x 3.7W channels into 3 ohm impedance speakers. Inside the miniature chip is a class D controller, able to run from 2.7V-5.5VDC. Since the amp is a class D, its incredibly efficient (over 90% efficient when driving an 8Ω speaker at over a Watt) - making it perfect for portable and battery-powered projects. It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
