# Fritzing sketch sequencer (saved by Fritzing 1.0.0rc)
breadboards: 1

parts:
  U3 = 4017 [chip_label=4017 package="DIP (Dual Inline) [THT]"]
  LED1 = LED - 3mm [color="Red (633nm)" current=0.030A package="3 mm [THT]"]
  R1 = Resistor [tolerance=±5% resistance=2.2k package="0603 [SMD]"]

nets:
  N1: U3.pin3, R1.Pin_1
  N2: U3.pin8, U3.pin13, LED1.cathode
  N3: U3.pin9, U3.pin15
  N4: LED1.anode, R1.Pin_0

notes:
  Flashes on step 0
  Outputs voltage on step 0
  Step 8 = Step 0
  Connected to the "clock"
  5
  1
  2
  6
  7
  3
  8
  4
  9

custom parts:
  4017: 4017 CMOS decade counter with 10 decoded outputs
