# Fritzing sketch vco (saved by Fritzing 1.0.0rc)
breadboards: 1

parts:
  U2 = 4046 [chip_label=4046 package="DIP (Dual Inline) [THT]"]
  R10 = Resistor [tolerance=±5% resistance=10k package="1206 [SMD]"]
  C2 = Capacitor [package=cap-pth-large]
  R11 = Rotary Potentiometer (Small) [maximum_resistance=10kΩ knob_status=50% power=0.5W package=THT]

nets:
  N1: U2.pin5, U2.pin8, R10.Pin_0, R11.leg2
  N2: U2.pin6, C2.1
  N3: U2.pin7, C2.2
  N4: U2.pin9, R11.wiper
  N5: U2.pin11, R10.Pin_1
  N6: U2.pin16, R11.leg1

custom parts:
  4046: 4017 CMOS decade counter with 10 decoded outputs
